// Logisim project assignment2.circ as structural Verilog
module p1_logic_gate (
  input  a,
  input  b,
  input  c,
  input  d,
  output out1,
  output out2
);

  logic_gate logic_gate_1 (.a(a), .b(b), .c(c), .d(d), .out1(out1), .out2(out2));

  // Notes on the sheet:
  //   Problem 1: out1 = a and b and c and d,  out2 = a or b or c or d
endmodule

module p2_mux8_1 (
  input  d0,
  input  d1,
  input  d2,
  input  d3,
  input  d4,
  input  d5,
  input  d6,
  input  d7,
  input  [2:0] ch,
  output data
);

  mux8_1 mux8_1_1 (.d0(d0), .d1(d1), .d2(d2), .d3(d3), .d4(d4), .d5(d5), .d6(d6), .d7(d7), .ch(ch), .data(data));

  // Notes on the sheet:
  //   Problem 2: 8-to-1 MUX  (ch = 000..111 selects d0..d7)
endmodule

module p3_led_letter (
  input  en,
  input  [2:0] sel
);

  wire a, b, c, d, dp, e, f, g;

  led_letter led_letter_1 (.en(en), .sel(sel), .display({a, b, c, d, e, f, g, dp}));
  _7_Segment_Display u_7_segment_display_1 (.g(g), .f(f), .a(a), .b(b), .e(e), .d(d), .c(c), .dp(dp));

  // Notes on the sheet:
  //   Problem 3: 7-segment letters  sel 000=A 001=b 010=C 011=d 100=F 101=g  (en=0: off)
endmodule

module p4_vote25 (
  input  [24:0] vt,
  output result
);

  vote25 vote25_1 (.vt(vt), .result(result));

  // Notes on the sheet:
  //   Problem 4: 25-person voting machine  (result = 1 if 13 or more votes)
endmodule

module p5_count13_led (
  input  en,
  input  [12:0] vt
);

  wire a, b, c, d, dp, e, f, g;

  count13_led count13_led_1 (.en(en), .vt(vt), .display({a, b, c, d, e, f, g, dp}));
  _7_Segment_Display u_7_segment_display_1 (.g(g), .f(f), .a(a), .b(b), .e(e), .d(d), .c(c), .dp(dp));

  // Notes on the sheet:
  //   Problem 5: number of '1's in vt(13 bits) -> 0-9, A-F on 7-segment  (en=0: off)
endmodule

// VHDL entity logic_gate, as the project stores it:
library ieee;
use ieee.std_logic_1164.all;
use ieee.std_logic_arith.all;
use ieee.std_logic_unsigned.all;

entity logic_gate is
    port(
        a, b, c, d : in  std_logic;
        out1       : out std_logic;
        out2       : out std_logic
    );
end entity logic_gate;

architecture bhv of logic_gate is
begin
    out1 <= a and b and c and d;
    out2 <= a or b or c or d;
end architecture bhv;

// VHDL entity mux8_1, as the project stores it:
library ieee;
use ieee.std_logic_1164.all;
use ieee.std_logic_arith.all;
use ieee.std_logic_unsigned.all;

entity mux8_1 is
    port(
        d0, d1, d2, d3, d4, d5, d6, d7 : in  std_logic;
        ch                             : in  std_logic_vector(2 downto 0);
        data                           : out std_logic
    );
end entity mux8_1;

architecture bhv of mux8_1 is
begin
    process(d0, d1, d2, d3, d4, d5, d6, d7, ch)
    begin
        case ch is
            when "000"  => data <= d0;
            when "001"  => data <= d1;
            when "010"  => data <= d2;
            when "011"  => data <= d3;
            when "100"  => data <= d4;
            when "101"  => data <= d5;
            when "110"  => data <= d6;
            when "111"  => data <= d7;
            when others => data <= '0';
        end case;
    end process;
end architecture bhv;

// VHDL entity led_letter, as the project stores it:
library ieee;
use ieee.std_logic_1164.all;
use ieee.std_logic_arith.all;
use ieee.std_logic_unsigned.all;

entity led_letter is
    port(
        en      : in  std_logic;
        sel     : in  std_logic_vector(2 downto 0);
        display : out std_logic_vector(7 downto 0)
    );
end entity led_letter;

architecture bhv of led_letter is
begin
    process(en, sel)
    begin
        if en = '0' then
            display <= "00000000";
        else
            case sel is
                when "000"  => display <= "11101110";
                when "001"  => display <= "00111110";
                when "010"  => display <= "10011100";
                when "011"  => display <= "01111010";
                when "100"  => display <= "10001110";
                when "101"  => display <= "11110110";
                when others => display <= "00000000";
            end case;
        end if;
    end process;
end architecture bhv;

// VHDL entity vote25, as the project stores it:
library ieee;
use ieee.std_logic_1164.all;
use ieee.std_logic_arith.all;
use ieee.std_logic_unsigned.all;

entity vote25 is
    port(
        vt     : in  std_logic_vector(25 downto 1);
        result : out std_logic
    );
end entity vote25;

architecture bhv of vote25 is
begin
    process(vt)
        variable sum : integer range 0 to 25;
    begin
        sum := 0;
        for i in 1 to 25 loop
            if vt(i) = '1' then
                sum := sum + 1;
            end if;
        end loop;

        if sum >= 13 then
            result <= '1';
        else
            result <= '0';
        end if;
    end process;
end architecture bhv;

// VHDL entity count13_led, as the project stores it:
library ieee;
use ieee.std_logic_1164.all;
use ieee.std_logic_arith.all;
use ieee.std_logic_unsigned.all;

entity count13_led is
    port(
        en      : in  std_logic;
        vt      : in  std_logic_vector(13 downto 1);
        display : out std_logic_vector(7 downto 0)
    );
end entity count13_led;

architecture bhv of count13_led is
begin
    process(en, vt)
        variable sum : integer range 0 to 15;
    begin
        sum := 0;
        for i in 1 to 13 loop
            if vt(i) = '1' then
                sum := sum + 1;
            end if;
        end loop;

        if en = '0' then
            display <= "00000000";
        else
            case sum is
                when 0      => display <= "11111100";
                when 1      => display <= "01100000";
                when 2      => display <= "11011010";
                when 3      => display <= "11110010";
                when 4      => display <= "01100110";
                when 5      => display <= "10110110";
                when 6      => display <= "10111110";
                when 7      => display <= "11100000";
                when 8      => display <= "11111110";
                when 9      => display <= "11100110";
                when 10     => display <= "11101110";
                when 11     => display <= "00111110";
                when 12     => display <= "10011100";
                when 13     => display <= "01111010";
                when 14     => display <= "10011110";
                when 15     => display <= "10001110";
                when others => display <= "00000000";
            end case;
        end if;
    end process;
end architecture bhv;
